// Logisim project rcd.circ as structural Verilog: 1 circuit, main circuit main
module main (
);

  wire clock_1_out;
  wire [7:0] counter_1_q;

  Clock clock_1 (.out(clock_1_out));
  Counter counter_1 (.Q(counter_1_q), .clk(clock_1_out));  // open: load, D, count, carry, clr
  ROM #(.dataWidth(32)) rom_1 (.addr(counter_1_q));  // open: data, sel
  RAM #(.addrWidth(4)) ram_1 (.clk(clock_1_out));  // open: addr, data, sel, ld, clr
  RAM ram_2 (.clk(clock_1_out));  // open: addr, data, sel, ld, clr
  RAM ram_3 (.clk(clock_1_out));  // open: addr, data, sel, ld, clr
endmodule
